# Fritzing sketch beetbox (saved by Fritzing 0.7.10b)
breadboards: 1

parts:
  U1 = LM386 [package=dip08]
  TRRS1 = Audio Jack (TRRS) 3.5mm [part_number="LUMBERG JEITA RC-5325A" package="RC-5325A [SMD]"]
  Part1 = MPR121 Breakout
  C1 = Electrolytic Capacitor [package=THT]
  C2 = Electrolytic Capacitor [package=THT]
  R1 = 10 Ω Resistor [package=THT]
  C5 = Ceramic Capacitor [package=THT]
  RaspberryPi2 = Raspberry Pi Model B
  SPKR1 = Loudspeaker

nets:
  N1: U1.+IN, TRRS1.SLEEVE, C1.-, R1.Pin_0, RaspberryPi2.GND, SPKR1.pin1
  N2: U1.V-, TRRS1.TIP
  N3: U1.BP, C1.+, RaspberryPi2.5V_2
  N4: Part1.GND, RaspberryPi2.GND_2
  VCC: Part1.VCC, RaspberryPi2.3V3
  N5: Part1.SCL, RaspberryPi2.SCL
  N6: Part1.SDA, Part1.ADD, RaspberryPi2.SDA
  N7: Part1.IRQ, RaspberryPi2.#4
  N8: C2.-, SPKR1.pin2
  N9: C2.+, C5.pin_1
  N10: R1.Pin_1, C5.pin_0

notes:
  To Beets.
  Optional LM386 Amp

custom parts:
  Raspberry Pi Model B: Raspberry Pi (Model B)
